# Fritzing sketch dog-motion-capture-system-diagram (saved by Fritzing 0.9.4)
breadboards: 2

parts:
  Componente1 = Arduino Mega 2560 (Rev3)
  Componente2 = InvenSense MPU6050
  Componente3 = InvenSense MPU6050
  VCC1 = Battery block 9V
  J1 = Basic Force Sensing Resistor (FSR) [package=THT]
  J2 = Basic Force Sensing Resistor (FSR) [package=THT]
  J3 = Basic Force Sensing Resistor (FSR) [package=THT]
  J4 = Basic Force Sensing Resistor (FSR) [package=THT]
  J5 = Basic Force Sensing Resistor (FSR) [package=THT]
  J6 = Basic Force Sensing Resistor (FSR) [package=THT]
  J7 = Basic Force Sensing Resistor (FSR) [package=THT]
  J8 = Basic Force Sensing Resistor (FSR) [package=THT]
  J9 = Basic Force Sensing Resistor (FSR) [package=THT]
  J10 = Basic Force Sensing Resistor (FSR) [package=THT]
  J11 = Basic Force Sensing Resistor (FSR) [package=THT]
  J12 = Basic Force Sensing Resistor (FSR) [package=THT]
  J13 = Basic Force Sensing Resistor (FSR) [package=THT]
  J14 = Basic Force Sensing Resistor (FSR) [package=THT]
  R1 = Resistor [tolerance=±5% resistance=220 package=THT]
  R2 = Resistor [tolerance=±5% resistance=220 package=THT]
  R3 = Resistor [tolerance=±5% resistance=220 package=THT]
  R4 = Resistor [tolerance=±5% resistance=220 package=THT]
  R5 = Resistor [tolerance=±5% resistance=220 package=THT]
  R6 = Resistor [tolerance=±5% resistance=220 package=THT]
  R7 = Resistor [tolerance=±5% resistance=220 package=THT]
  R8 = Resistor [tolerance=±5% resistance=220 package=THT]
  R9 = Resistor [tolerance=±5% resistance=220 package=THT]
  R10 = Resistor [tolerance=±5% resistance=220 package=THT]
  R11 = Resistor [tolerance=±5% resistance=220 package=THT]
  R12 = Resistor [tolerance=±5% resistance=220 package=THT]
  R13 = Resistor [tolerance=±5% resistance=220 package=THT]
  R14 = Resistor [tolerance=±5% resistance=220 package=THT]

nets:
  N1: Componente1.A8, J7.pin_1, R6.Pin_1
  N2: Componente1.A9, J6.pin_1, R5.Pin_1
  N3: Componente1.A10, J5.pin_1, R4.Pin_1
  N4: Componente1.A11, J4.pin_1, R3.Pin_1
  N5: Componente1.A12, J3.pin_1, R2.Pin_1
  N6: Componente1.A13, J2.pin_1, R1.Pin_1
  N7: Componente1.A0, J9.pin_1, R14.Pin_1
  N8: Componente1.A1, J12.pin_1, R13.Pin_1
  N9: Componente1.A2, J13.pin_1, R12.Pin_1
  N10: Componente1.A3, J11.pin_1, R11.Pin_1
  N11: Componente1.A4, J10.pin_1, R10.Pin_1
  N12: Componente1.A5, J14.pin_1, R9.Pin_1
  N13: Componente1.A6, J8.pin_1, R8.Pin_1
  N14: Componente1.A7, J1.pin_1, R7.Pin_1
  N15: Componente1.D21/SCL, Componente2.SCL, Componente3.SCL
  N16: Componente1.D20/SDA, Componente2.SDA, Componente3.SDA
  GND: Componente1.GND, Componente2.GND, Componente3.GND, VCC1.-
  VCC: Componente1.3V3, Componente2.VCC, Componente3.VCC
  N17: Componente1.5V, J1.pin_0, J2.pin_0, J3.pin_0, J4.pin_0, J5.pin_0, J6.pin_0, J7.pin_0, J8.pin_0, J9.pin_0, J10.pin_0, J11.pin_0, J12.pin_0, J13.pin_0, J14.pin_0
  N18: Componente1.VIN, VCC1.+
